# Fritzing sketch connections (saved by Fritzing 0.9.3b)

parts:
  U1 = NodeMCU V3.0
  LED1 = LEDs [package=led10mm]
  R1 = Resistor [tolerance=±5% resistance=220 package=THT]
  S1 = Pushbutton [package="[SMD]"]

nets:
  N1: U1.D1, S1.Pin_3, S1.Pin_4
  N2: U1.D2, LED1.C
  N3: U1.GND, R1.Pin_1, S1.Pin_2
  N4: LED1.A, R1.Pin_0

custom parts:
  NodeMCU V3.0: ESP8266 based NodeMCU
