# Fritzing sketch connections (saved by Fritzing 0.9.3b)

parts:
  U1 = NodeMCU V3.0
  LED1 = LEDs [package=led10mm]  # not connected
  R1 = Resistor [tolerance=±5% resistance=220 package=THT]
  Part2 = HC-SR501 Body Sensor Module

nets:
  GND: U1.GND, R1.Pin_1, Part2.GND
  N1: U1.D5, Part2.OUT
  VIN: U1.Vin, Part2.VCC

custom parts:
  NodeMCU V3.0: ESP8266 based NodeMCU
  HC-SR501 Body Sensor Module: Pyroelectric Infrared PIR Motion Sensor Detector Module
