# Fritzing sketch connections (saved by Fritzing 0.9.3b)

parts:
  U1 = NodeMCU V3.0
  LED1 = LEDs [package=led10mm]
  R1 = Resistor [tolerance=±5% resistance=220 package=THT]

nets:
  N1: U1.D1, LED1.C
  N2: U1.GND, R1.Pin_1
  N3: LED1.A, R1.Pin_0

custom parts:
  NodeMCU V3.0: ESP8266 based NodeMCU
