# Fritzing sketch connections (saved by Fritzing 0.9.3b)

parts:
  WeMos_D1_Mini1 = WeMos D1 Mini
  Part2 = BME280 Breakout

nets:
  3V3: WeMos_D1_Mini1.3V3, Part2.3.3V
  N1: WeMos_D1_Mini1.D1, Part2.SCK/SCL
  N2: WeMos_D1_Mini1.D2, Part2.SDI/SDA
  N3: WeMos_D1_Mini1.G, Part2.GND
