# Fritzing sketch connections (saved by Fritzing 0.9.3b)
circuit board: 6.3cm x 4.9cm

parts:
  M1 = BMP280
  OLED1 = OLED 128x64 I2C Monochrome Display
  S1 = Pushbutton [package="[SMD]"]
  WeMos_D1_Mini1 = WeMos D1 Mini

nets:
  VIN: M1.VIN, OLED1.VDD, WeMos_D1_Mini1.3V3
  GND: M1.GND, OLED1.GND, WeMos_D1_Mini1.G
  N1: M1.SCL, OLED1.SCK, WeMos_D1_Mini1.D1
  N2: M1.SDA, OLED1.SDA, WeMos_D1_Mini1.D2
  N3: S1.Pin_3, S1.Pin_4, WeMos_D1_Mini1.D3

notes:
  GND

custom parts:
  BMP280: Temperature Humidity Barometric presure Sensor, I2C
