# Fritzing sketch connections (saved by Fritzing 0.9.3b)

parts:
  LED1 = LEDs [package=led10mm]
  R1 = Resistor [tolerance=±5% resistance=220 package=THT]  # not connected
  ESP32-CAM1 = ESP32-CAM
  Part2 = HC-SR501 Body Sensor Module
  Power_plug1 = Power plug

nets:
  N1: LED1.A, ESP32-CAM1.GPIO12, Part2.OUT
  VCC: ESP32-CAM1.5V, Part2.VCC, Power_plug1.VCC
  GND: ESP32-CAM1.GND, Part2.GND, Power_plug1.GND

custom parts:
  ESP32-CAM: AIThinker
  HC-SR501 Body Sensor Module: Pyroelectric Infrared PIR Motion Sensor Detector Module
