# Fritzing sketch connections (saved by Fritzing 0.9.3b)

parts:
  MCU1 = Raspberry Pi Zero
  J1 = Basic Servo
  Part3 = 16-Channel 12-bit PWM Servo Driver - I2C [part_number=815]
  J2 = Basic Servo
  Power_plug1 = Power plug
  Power_plug2 = Power plug
  M3 = DC Motor
  M4 = DC Motor
  Part4 = Motor Driver 1A Dual TB6612FNG
  M2 = DC Motor
  M1 = DC Motor

nets:
  N1: MCU1.pin_2, MCU1.pin_4, Part4.STBY
  N2: MCU1.pin_3, Part3.SDA
  N3: MCU1.pin_5, Part3.SCL
  N4: MCU1.pin_16, Part4.BIN2
  N5: MCU1.pin_18, Part4.BIN1
  N6: MCU1.pin_22, Part4.AIN1
  N7: MCU1.pin_24, Part4.AIN2
  GND: J1.gnd, Part3.GND, J2.gnd, Power_plug1.GND, Power_plug2.GND, Part4.GND
  VCC: J1.vcc, Part3.5.0V, J2.vcc
  N8: J1.pulse, Part3.PWM0
  N9: Part3.PWM1, J2.pulse
  N10: Part3.PWM15, Part4.PWMB
  N11: Part3.PWM14, Part4.PWMA
  VCC_2: Power_plug1.VCC, Part4.VCC
  N12: Power_plug2.VCC, Part4.VM
  N13: M3.pin_1, M4.pin_1, Part4.A01
  N14: M3.pin_2, M4.pin_2, Part4.A02
  N15: Part4.B01, M2.pin_2, M1.pin_2
  N16: Part4.B02, M2.pin_1, M1.pin_1

notes:
  +5V
  +6V

custom parts:
  16-Channel 12-bit PWM Servo Driver - I2C: You want to make a cool robot, maybe a hexapod walker, or maybe just a piece of art with a lot of moving parts. Or maybe you want to drive a lot of LEDs with precise PWM output. Using only two pins, control 16 free-running PWM outputs! You can even chain up 62 breakouts to control up to 992 PWM outputs.
