# Fritzing sketch connections (saved by Fritzing 0.9.3b)

parts:
  LED1 = LEDs [package=led10mm]
  R1 = Resistor [tolerance=±5% resistance=220 package=THT]
  MCU1 = Raspberry Pi Zero

nets:
  N1: LED1.C, MCU1.pin_12
  N2: LED1.A, R1.Pin_0
  N3: R1.Pin_1, MCU1.pin_14, MCU1.pin_39
